# Fritzing sketch RobotHeadToy (saved by Fritzing 0.5.0b)
breadboards: 1

parts:
  Arduino1 = Arduino
  LED1 = Red LED - 5mm
  R1 = Rotary Potentiometer (Large) [package=THT]
  R2 = Rotary Potentiometer (Large) [package=THT]
  LED1_2 = Red LED - 5mm
  LED1_3 = Red LED - 5mm
  LED1_4 = Red LED - 5mm
  S1 = Pushbutton [package=THT]
  S1_2 = Pushbutton [package=THT]
  R3 = 220 Ω Resistor [package=THT]
  R3_2 = 220 Ω Resistor [package=THT]
  R3_3 = 220 Ω Resistor [package=THT]
  R3_4 = 220 Ω Resistor [package=THT]
  R3_5 = 220 Ω Resistor [package=THT]
  R3_6 = 220 Ω Resistor [package=THT]
  J1 = Piezo Speaker
  LED1_5 = Red LED - 5mm
  LED1_6 = Red LED - 5mm
  R3_7 = 220 Ω Resistor [package=THT]
  R3_8 = 220 Ω Resistor [package=THT]
  R3_9 = 220 Ω Resistor [package=THT]
  R3_10 = 220 Ω Resistor [package=THT]
  R4 = Slide Potentiometer
  R5 = Slide Potentiometer
  S2 = Pushbutton [package=THT]
  R6 = Slide Potentiometer
  LED2 = RGB LED - (4 legs) [package="5 mm [THT]"]

nets:
  N1: Arduino1.D13, Arduino1.D6, S1.leg0, R3.Pin_1, S2.leg1
  N2: Arduino1.D12, S1_2.leg0
  N3: Arduino1.D11, R3_10.Pin_1
  N4: Arduino1.D10, R3_9.Pin_1
  N5: Arduino1.D9, R3_6.Pin_1
  N6: Arduino1.D8, R3_5.Pin_1
  N7: Arduino1.D7, R3_4.Pin_1
  N8: Arduino1.D5, R3_3.Pin_1
  N9: Arduino1.D4, R3_2.Pin_1
  N10: Arduino1.D3, R3_7.Pin_1
  N11: Arduino1.D2, R3_8.Pin_1
  N12: Arduino1.+5V, R1.leg2, R2.leg2, R4.leg2, R5.leg2, R6.leg2, LED2.red_cathode
  N13: Arduino1.GND, LED1.cathode, R1.leg1, R2.leg1, LED1_2.cathode, LED1_3.cathode, LED1_4.cathode, S1.leg1, S1_2.leg1, J1.pin1, LED1_5.cathode, LED1_6.cathode, R4.leg1, R5.leg1, S2.leg0, R6.leg1
  N14: Arduino1.A0, R1.wiper
  N15: Arduino1.A1, R4.wiper
  N16: Arduino1.A2, R5.wiper
  N17: Arduino1.A3, R6.wiper
  N18: Arduino1.A4, R2.wiper
  N19: LED1.anode, R3_2.Pin_0
  N20: LED1_2.anode, R3_3.Pin_0
  N21: LED1_3.anode, R3_4.Pin_0
  N22: LED1_4.anode, R3_5.Pin_0
  N23: R3.Pin_0, J1.pin2
  N24: R3_6.Pin_0, LED2.blue_cathode
  N25: LED1_5.anode, R3_7.Pin_0
  N26: LED1_6.anode, R3_8.Pin_0
  N27: R3_9.Pin_0, LED2.green_cathode
  N28: R3_10.Pin_0, LED2.common_anode
